// Logisim project NSF_Board.circ as structural Verilog: 5 circuits, main circuit main
module main (
);

  wire apu_1_aux_a, apu_1_aux_b, apu_1_m2, apu_1_n_in0, apu_1_n_in1, apu_1_out0, apu_1_out1, apu_1_out2,
       apu_1_rnw, aux_dumper_1_tofile, button_1_out, clock_1_out, nor_1_out, not_1_out;
  wire [7:0] apu_1_db_out, wram_1_db_out;
  wire [15:0] apu_1_a;

  Clock clock_1 (.out(clock_1_out));
  Button button_1 (.out(button_1_out));
  APU apu_1 (
    .CLK(clock_1_out), .n_RES(button_1_out), .n_NMI(1'b1), .n_IRQ(1'b1), .DBG(1'b0), .DB_In(wram_1_db_out),
    .AUX_A(apu_1_aux_a), .AUX_B(apu_1_aux_b), .A(apu_1_a), .M2(apu_1_m2), .RnW(apu_1_rnw), .OUT0(apu_1_out0),
    .OUT1(apu_1_out1), .OUT2(apu_1_out2), .n_IN0(apu_1_n_in0), .n_IN1(apu_1_n_in1), .DB_Out(apu_1_db_out));
  // NoConnect on apu_1_m2
  // NoConnect on apu_1_out0
  // NoConnect on apu_1_out1
  // NoConnect on apu_1_out2
  // NoConnect on apu_1_n_in0
  // NoConnect on apu_1_n_in1
  nor nor_1 (nor_1_out, apu_1_a[11], apu_1_a[12], apu_1_a[13], apu_1_a[14], apu_1_a[15]);
  not not_1 (not_1_out, nor_1_out);
  WRAM wram_1 (.Addr(apu_1_a[10:0]), .RnW(apu_1_rnw), .CS(nor_1_out), .DB_In(apu_1_db_out), .DB_Out(wram_1_db_out));
  Banked_SRAM banked_sram_1 (
    .Addr(apu_1_a), .RnW(apu_1_rnw), .CS(not_1_out), .DB_In(apu_1_db_out), .DB_Out(wram_1_db_out));
  AUX_Dumper aux_dumper_1 (.AUX_A(apu_1_aux_a), .AUX_B(apu_1_aux_b), .ToFile(aux_dumper_1_tofile));

  // Notes on the sheet:
  //   C# App
  //   <--- NSF Data here
endmodule

module Banked_SRAM (
  input  [15:0] Addr,
  input  RnW,
  input  CS,
  input  [7:0] DB_In,
  output [7:0] DB_Out
);
endmodule

module APU (
  input  CLK,
  input  n_RES,
  input  n_NMI,
  input  n_IRQ,
  input  DBG,
  input  [7:0] DB_In,
  output AUX_A,
  output AUX_B,
  output [15:0] A,
  output M2,
  output RnW,
  output OUT0,
  output OUT1,
  output OUT2,
  output n_IN0,
  output n_IN1,
  output [7:0] DB_Out
);


  assign A = {16{1'b0}};
endmodule

module AUX_Dumper (
  input  AUX_A,
  input  AUX_B,
  output ToFile
);
endmodule

module WRAM (
  input  [10:0] Addr,
  input  RnW,
  input  CS,
  input  [7:0] DB_In,
  output [7:0] DB_Out
);
endmodule
